# Fritzing sketch diagram (saved by Fritzing 0.9.3b)

parts:
  Part1 = Arduino Uno (Rev3)
  Power_12v = Power plug  # not connected
  Ventilateur_12V = Fan - Ventilador [package=THT]
  OLED_Display = Grove OLED 128x96
  DHT11 = Humidity and Temperature Sensor RHT03 [part_number="Temp&Humidity Sensor"]
  Relay = Keyes Relay [package=THT]

nets:
  N1: Part1.A4/SDA, OLED_Display.SDA
  N2: Part1.A5/SCL, OLED_Display.SCL
  N3: Part1.D2, DHT11.Data-signal
  N4: Part1.D3_PWM, Relay.signal
  VCC: Part1.5V, OLED_Display.VCC, DHT11.Vcc, Relay.power
  GND: Part1.GND, OLED_Display.GND, DHT11.GND_2, Relay.ground
  N5: Ventilateur_12V.5V, Relay.NO

custom parts:
  Fan - Ventilador: Ventilador de 2 pines, se encuentra comunmente en computadoras de escritorio
  Keyes Relay: The Keyes 5V relay module is suitable for SCM development, home appliance control. It uses a 5V~12V TIL control signal which can control DC / AC signal.
